// Logisim project cpu.circ as structural Verilog: 2 circuits, main circuit main
module main (
  input  [15:0] INSTRUCTION,
  input  CLOCK,
  output [15:0] FETCH_ADDRESS,
  output [15:0] L_s0_Value_7c9fba82,
  output [15:0] L_s1_Value_2cb75696,
  output [15:0] L_s2_Value_be7b1681,
  output [15:0] L_ra_Value_55886cf9,
  output [15:0] L_sp_Value_a0856b3d,
  output [15:0] L_HI_Value_3bde5b98,
  output [15:0] L_LO_Value_b62659ce
);

  wire EQUAL, WRITE_EN_HI, WRITE_EN_LO, WRITE_EN_RAM, WRITE_EN_REG;
  wire [2:0] REG_ADDR_R1, REG_ADDR_R2, REG_ADDR_WR, SWITCH;
  wire [15:0] ALU_RESULT, control_unit_cpu_1_alu_x, control_unit_cpu_1_alu_y, NEXT_ADDR, RAM_ADDR, RAM_READ,
       REG_READ_1, REG_READ_2, WRITE_HI, WRITE_LO, WRITE_RAM, WRITE_REG;

  Register #(.width(16)) L_PC_bd1e00e6 (.D(NEXT_ADDR), .en(1'b1), .clk(CLOCK), .Q(FETCH_ADDRESS));  // open: clr
  Register #(.width(16)) L_LO_ba622f5d (
    .D(WRITE_LO), .en(WRITE_EN_LO), .clk(CLOCK), .Q(L_LO_Value_b62659ce));  // open: clr
  Register #(.width(16)) L_HI_1d3f3066 (
    .D(WRITE_HI), .en(WRITE_EN_HI), .clk(CLOCK), .Q(L_HI_Value_3bde5b98));  // open: clr
  regfile_main main_1 (
    .L_s1_Value_f16d02bf(L_s1_Value_2cb75696), .L_ra_Value_b804995d(L_ra_Value_55886cf9),
    .Read_Data_1_c47ea0d8(REG_READ_1), .Read_Register_1_eca808b4(REG_ADDR_R1),
    .Write_Register_1c78e1ef(REG_ADDR_WR), .Write_Enable_5f560963(WRITE_EN_REG),
    .Write_Data_00073c80(WRITE_REG), .Read_Register_2_4b336a3e(REG_ADDR_R2),
    .Read_Data_2_34b29906(REG_READ_2), .L_sp_Value_269f0ffd(L_sp_Value_a0856b3d),
    .L_s2_Value_6a9ed51f(L_s2_Value_be7b1681), .L_s0_Value_3e1de553(L_s0_Value_7c9fba82), .Clock(CLOCK));
  // mem_main MEM: pin names not known; wires that end beside it: RAM_ADDR, WRITE_RAM, WRITE_EN_RAM, CLOCK, RAM_READ
  CONTROL_UNIT_CPU control_unit_cpu_1 (
    .PC(FETCH_ADDRESS), .EQUAL(EQUAL), .REG_READ_1(REG_READ_1), .REG_READ_2(REG_READ_2), .RAM_READ(RAM_READ),
    .HI_READ(L_HI_Value_3bde5b98), .INSTR(INSTRUCTION), .LO_READ(L_LO_Value_b62659ce),
    .ALU_RESULT(ALU_RESULT), .WRITE_EN_RAM(WRITE_EN_RAM), .WRITE_EN_REG(WRITE_EN_REG), .ALU_SWITCH(SWITCH),
    .ALU_X(control_unit_cpu_1_alu_x), .ALU_Y(control_unit_cpu_1_alu_y), .RAM_ADDR(RAM_ADDR),
    .REG_ADDR_R1(REG_ADDR_R1), .REG_ADDR_R2(REG_ADDR_R2), .REG_ADDR_WR(REG_ADDR_WR), .FETCH_ADDR(NEXT_ADDR),
    .WRITE_EN_HI(WRITE_EN_HI), .WRITE_EN_LO(WRITE_EN_LO), .WRITE_RAM(WRITE_RAM), .WRITE_REG(WRITE_REG),
    .WRITE_LO(WRITE_LO));
  alu_main main_2 (
    .Equal(EQUAL), .Result(ALU_RESULT), .Result_2_a9898de3(WRITE_HI), .X(control_unit_cpu_1_alu_x),
    .Y(control_unit_cpu_1_alu_y), .Switch(SWITCH));

  // Other names for the same wires on the sheet: clk = CLOCK; fetch_addr[15:0] = FETCH_ADDRESS;
  //   HI[15:0] = L_HI_Value_3bde5b98; LO[15:0] = L_LO_Value_b62659ce

  // Notes on the sheet:
  //   Output
  //   These are outputs/inputs from run.circ
  //   Inputs
  //   These are DEBUG/TEST outputs from your circuit.
endmodule

module CONTROL_UNIT_CPU (
  input  [15:0] PC,
  input  EQUAL,
  input  [15:0] REG_READ_1,
  input  [15:0] REG_READ_2,
  input  [15:0] RAM_READ,
  input  [15:0] HI_READ,
  input  [15:0] INSTR,
  input  [15:0] LO_READ,
  input  [15:0] ALU_RESULT,
  output WRITE_EN_RAM,
  output WRITE_EN_REG,
  output [2:0] ALU_SWITCH,
  output [15:0] ALU_X,
  output [15:0] ALU_Y,
  output [15:0] RAM_ADDR,
  output [2:0] REG_ADDR_R1,
  output [2:0] REG_ADDR_R2,
  output [2:0] REG_ADDR_WR,
  output [15:0] FETCH_ADDR,
  output WRITE_EN_HI,
  output WRITE_EN_LO,
  output [15:0] WRITE_RAM,
  output [15:0] WRITE_REG,
  output [15:0] WRITE_LO
);

  wire and_1_out, demultiplexer_1_out1, demultiplexer_1_out2, demultiplexer_1_out4, demultiplexer_1_out5,
       demultiplexer_1_out7, demultiplexer_1_out8, demultiplexer_1_out9, demultiplexer_2_out0,
       demultiplexer_2_out1, demultiplexer_2_out4, demultiplexer_2_out5, demultiplexer_2_out7,
       demultiplexer_4_out1, demultiplexer_4_out2, demultiplexer_4_out3, demultiplexer_4_out10,
       demultiplexer_4_out11, demultiplexer_4_out12, demultiplexer_4_out13, MEM, not_1_out, not_2_out,
       ON_BRANCH, or_3_out, or_5_out, TYPE_R, TYPE_U;
  wire [2:0] multiplexer_1_out, multiplexer_19_out;
  wire [3:0] controlled_buffer_1_out;
  wire [15:0] adder_3_out, bit_extender_1_out, bit_extender_2_out, bit_extender_3_out, bit_extender_4_out,
       BRANCH_ADDR, multiplexer_3_out, multiplexer_4_out, multiplexer_6_out, multiplexer_7_out,
       multiplexer_8_out, multiplexer_10_out, multiplexer_11_out, PCPLUS2, shifter_1_out;

  assign bit_extender_1_out = {{10{INSTR[5]}}, INSTR[5:0]};  // Bit_Extender bit_extender_1
  Multiplexer #(.select(4), .width(3), .enable("false")) multiplexer_1 (
    .in0(3'b000), .in1(3'b000), .in2(3'b000), .in3(3'b000), .in4(3'b000), .in5(3'b000), .in6(3'b010),
    .in7(3'b110), .in8(3'b011), .in9(3'b100), .in10(3'b010), .in11(3'b010), .in12(3'b000), .in13(3'b000),
    .in14(3'b000), .in15(3'b000), .out(multiplexer_1_out), .sel(INSTR[15:12]));
  Adder #(.width(16)) adder_1 (.a(PC), .b(bit_extender_1_out), .out(BRANCH_ADDR));  // open: cin, cout
  Adder #(.width(16)) adder_2 (.a(PC), .b(16'h2), .out(PCPLUS2));  // open: cin, cout
  Multiplexer #(.width(3), .enable("false")) multiplexer_2 (
    .in0(multiplexer_1_out), .in1(INSTR[2:0]), .out(ALU_SWITCH), .sel(TYPE_R));
  Multiplexer #(.width(16), .enable("false")) multiplexer_3 (
    .in0(BRANCH_ADDR), .in1(PCPLUS2), .out(multiplexer_3_out), .sel(EQUAL));
  assign bit_extender_2_out = {{10{INSTR[5]}}, INSTR[5:0]};  // Bit_Extender bit_extender_2
  Multiplexer #(.width(16), .enable("false")) multiplexer_4 (
    .in0(PCPLUS2), .in1(BRANCH_ADDR), .out(multiplexer_4_out), .sel(EQUAL));
  Adder #(.width(16)) adder_3 (.a(REG_READ_1), .b(bit_extender_2_out), .out(adder_3_out));  // open: cin, cout
  Demultiplexer #(.select(4), .enable("false")) demultiplexer_1 (
    .out0(TYPE_R), .out1(demultiplexer_1_out1), .out2(demultiplexer_1_out2), .out4(demultiplexer_1_out4),
    .out5(demultiplexer_1_out5), .out7(demultiplexer_1_out7), .out8(demultiplexer_1_out8),
    .out9(demultiplexer_1_out9), .in(1'b1), .sel(INSTR[15:12]));  // open: out3, out6, out10, out11, out12, out13, out14, out15
  Multiplexer #(.select(4), .width(16), .enable("false")) multiplexer_5 (
    .in0(PCPLUS2), .in1(PCPLUS2), .in2({PC[15:10], INSTR[9:0]}), .in3(adder_3_out), .in4(multiplexer_4_out),
    .in5(multiplexer_3_out), .in6(PCPLUS2), .in7(PCPLUS2), .in8(PCPLUS2), .in9(PCPLUS2), .in10(PCPLUS2),
    .in11(PCPLUS2), .in12(PCPLUS2), .in13(PCPLUS2), .in14(PCPLUS2), .in15(PCPLUS2), .out(FETCH_ADDR),
    .sel(INSTR[15:12]));
  assign bit_extender_3_out = {{10{INSTR[5]}}, INSTR[5:0]};  // Bit_Extender bit_extender_3
  or or_1 (TYPE_U, demultiplexer_1_out1, demultiplexer_1_out2);
  or or_2 (ON_BRANCH, demultiplexer_1_out4, demultiplexer_1_out5);
  or or_3 (or_3_out, demultiplexer_1_out8, demultiplexer_1_out9);
  Demultiplexer #(.select(3), .enable("false")) demultiplexer_2 (
    .out0(demultiplexer_2_out0), .out1(demultiplexer_2_out1), .out4(demultiplexer_2_out4),
    .out5(demultiplexer_2_out5), .out7(demultiplexer_2_out7), .in(TYPE_R), .sel(INSTR[2:0]));  // open: out2, out3, out6
  Multiplexer #(.width(16), .enable("false")) multiplexer_6 (
    .in0(bit_extender_3_out), .in1({{10{1'b0}}, INSTR[5:0]}), .out(multiplexer_6_out), .sel(or_3_out));
  Demultiplexer #(.select(3), .enable("false")) demultiplexer_3 (
    .out7(WRITE_EN_HI), .in(TYPE_R), .sel(INSTR[2:0]));  // open: out0, out1, out2, out3, out4, out5, out6
  Demultiplexer #(.select(4), .enable("false")) demultiplexer_4 (
    .out1(demultiplexer_4_out1), .out2(demultiplexer_4_out2), .out3(demultiplexer_4_out3),
    .out10(demultiplexer_4_out10), .out11(demultiplexer_4_out11), .out12(demultiplexer_4_out12),
    .out13(demultiplexer_4_out13), .in(1'b1), .sel(INSTR[15:12]));  // open: out0, out4, out5, out6, out7, out8, out9, out14, out15
  Multiplexer #(.width(16), .enable("false")) multiplexer_7 (
    .in0(ALU_RESULT), .in1(PCPLUS2), .out(multiplexer_7_out), .sel(or_5_out));
  Multiplexer #(.width(16), .enable("false")) multiplexer_8 (
    .in0(multiplexer_7_out), .in1(RAM_READ), .out(multiplexer_8_out), .sel(demultiplexer_4_out10));
  Multiplexer #(.width(16), .enable("false")) multiplexer_9 (
    .in0(REG_READ_1), .in1(REG_READ_2), .out(ALU_X), .sel(MEM));
  Multiplexer #(.width(16), .enable("false")) multiplexer_10 (
    .in0(multiplexer_6_out), .in1(REG_READ_2), .out(multiplexer_10_out), .sel(TYPE_R));
  or or_4 (WRITE_EN_LO, WRITE_EN_HI, demultiplexer_4_out1);
  or or_5 (or_5_out, demultiplexer_4_out2, demultiplexer_4_out3);
  Multiplexer #(.width(16), .enable("false")) multiplexer_11 (
    .in0(multiplexer_8_out), .in1(HI_READ), .out(multiplexer_11_out), .sel(demultiplexer_4_out12));
  not not_1 (not_1_out, demultiplexer_2_out7);
  Multiplexer #(.width(16), .enable("false")) multiplexer_12 (
    .in0(multiplexer_11_out), .in1(LO_READ), .out(WRITE_REG), .sel(demultiplexer_4_out13));
  and and_1 (and_1_out, not_1_out, demultiplexer_1_out7);
  Multiplexer #(.select(4), .enable("false")) multiplexer_13 (
    .in0(1'b0), .in1(1'b0), .in2(1'b0), .in3(1'b0), .in4(1'b0), .in5(1'b0), .in6(1'b0), .in7(1'b0),
    .in8(1'b0), .in9(1'b0), .in10(1'b0), .in11(1'b1), .in12(1'b0), .in13(1'b0), .in15(1'b0),
    .out(WRITE_EN_RAM), .sel(INSTR[15:12]));  // open: in14
  or or_6 (MEM, demultiplexer_4_out10, demultiplexer_4_out11);
  assign controlled_buffer_1_out = TYPE_R ? {1'b0, INSTR[2:0]} : 4'bz;  // Controlled_Buffer controlled_buffer_1
  Multiplexer #(.select(4), .enable("false")) multiplexer_14 (
    .in0(demultiplexer_2_out0), .in1(demultiplexer_2_out1), .in2(1'b1), .in3(1'b1),
    .in4(demultiplexer_2_out4), .in5(demultiplexer_2_out5), .in6(1'b1), .in7(and_1_out), .in8(1'b1),
    .in9(1'b1), .in10(1'b1), .in11(1'b0), .in12(1'b1), .in13(1'b1), .in14(1'b0), .in15(1'b0),
    .out(WRITE_EN_REG), .sel(controlled_buffer_1_out));
  not not_2 (not_2_out, TYPE_R);
  assign controlled_buffer_1_out = not_2_out ? INSTR[15:12] : 4'bz;  // Controlled_Buffer controlled_buffer_2
  Multiplexer #(.width(16), .enable("false")) multiplexer_15 (
    .in0(multiplexer_10_out), .in1(REG_READ_2), .out(ALU_Y), .sel(ON_BRANCH));
  Multiplexer #(.width(3), .enable("false")) multiplexer_16 (
    .in0(INSTR[11:9]), .in1({1'b0, INSTR[11:10]}), .out(REG_ADDR_WR), .sel(TYPE_U));
  Multiplexer #(.width(3), .enable("false")) multiplexer_17 (
    .in0(INSTR[8:6]), .in1(INSTR[11:9]), .out(REG_ADDR_R1), .sel(MEM));
  Multiplexer #(.width(16), .enable("false")) multiplexer_18 (
    .in0(ALU_RESULT), .in1(shifter_1_out), .out(WRITE_LO), .sel(demultiplexer_4_out1));
  Multiplexer #(.width(3), .enable("false")) multiplexer_19 (
    .in0(INSTR[5:3]), .in1(INSTR[11:9]), .out(multiplexer_19_out), .sel(ON_BRANCH));
  Multiplexer #(.width(3), .enable("false")) multiplexer_20 (
    .in0(multiplexer_19_out), .in1(INSTR[8:6]), .out(REG_ADDR_R2), .sel(MEM));
  assign bit_extender_4_out = {{6{1'b0}}, INSTR[9:0]};  // Bit_Extender bit_extender_4
  Shifter #(.width(16)) shifter_1 (.in(bit_extender_4_out), .\dist (4'b0110), .out(shifter_1_out));

  assign RAM_ADDR = ALU_RESULT;
  assign WRITE_RAM = REG_READ_1;

  // Other names for the same wires on the sheet: IMME_I[5:0] = INSTR[5:0]; IMME_U[9:0] = INSTR[9:0];
  //   JUMP[15:0] = {PC[15:10], INSTR[9:0]}; RT_ADDR[2:0] = INSTR[5:3]; FUNCT[2:0] = INSTR[2:0];
  //   RS_ADDR[2:0] = INSTR[8:6]; RD_ADDR[2:0] = INSTR[11:9]; OPCODE[3:0] = INSTR[15:12]; RDU_ADDR[1:0] = INSTR[11:10]

  // Notes on the sheet:
  //   CALCULATE PC ADDRESS ON JUMP
  //   CALCULATE BRANCH ADDRESS ON BEQ AND BNE
  //   ALU RESULT IS ALSO USED TO ACESS MEMORY ADDRESS
  //   CALCULATE PC + 2
  //   SELECT OPCODE
  //   CALCULATE NEXT PC ADDRESS
  //   0 = type R
  //   1 OR 2 = type U
  //   SELECT OPCODE
  //   SELECT SIGN EXTENSION FOR IMMEDIATE
  //   SPLIT DATA FROM THE INSTRUCTION
  //   SELECT FUNCT
  //   SELECT VALUE TO WRITE IN REG
  //   SELECT ALU X
  //   SELECT ALU SWITCH
  //   SELECT WRITE ENABLE HI / LO
  //   SELECT WRITE ENABLE RAM
  //   SELECT WRITE ENABLE REG
  //   SELECT REG_R1 TO READ
  //   SELECT WRITE REGISTER
  //   SELECT REG_R2 TO READ
  //   On r-type,  X is rs and Y is rt
  //   GET DATA TO WRITE IN LO
endmodule
