// Logisim project alu.circ as structural Verilog: 1 circuit, main circuit main
module main (
  input  [15:0] X,
  input  [15:0] Y,
  input  [2:0] Switch,
  output Equal,
  output [15:0] Result,
  output [15:0] Result_2_a9898de3
);

  wire comparator_1_lt;
  wire [15:0] adder_1_out, and_1_out, and_2_out, bit_extender_3_out, multiplier_1_out, not_1_out, or_1_out,
       shifter_1_out, shifter_2_out, subtractor_1_out, xor_1_out;
  wire [31:0] bit_extender_1_out, bit_extender_2_out;

  assign bit_extender_1_out = {{16{X[15]}}, X};  // Bit_Extender bit_extender_1
  assign bit_extender_2_out = {{16{Y[15]}}, Y};  // Bit_Extender bit_extender_2
  Shifter #(.width(16)) shifter_1 (.in(X), .\dist (Y[3:0]), .out(shifter_1_out));
  Shifter #(.shift("lr"), .width(16)) shifter_2 (.in(X), .\dist (Y[3:0]), .out(shifter_2_out));
  Adder #(.width(16)) adder_1 (.a(X), .b(Y), .out(adder_1_out));  // open: cin, cout
  assign and_1_out = X & Y;  // AND_Gate and_1, 16 bits wide
  assign or_1_out = X | Y;  // OR_Gate or_1, 16 bits wide
  assign xor_1_out = X ^ Y;  // XOR_Gate xor_1, 16 bits wide
  Comparator #(.width(16)) comparator_1 (.a(X), .b(Y), .eq(Equal), .lt(comparator_1_lt));  // open: gt
  Multiplier #(.mode("twosComplement"), .width(32)) multiplier_1 (
    .a(bit_extender_1_out), .b(bit_extender_2_out), .out({Result_2_a9898de3, multiplier_1_out}));  // open: cin, cout
  Subtractor #(.width(16)) subtractor_1 (.a(X), .b(Y), .out(subtractor_1_out));  // open: bin, bout
  assign bit_extender_3_out = {{15{1'b0}}, comparator_1_lt};  // Bit_Extender bit_extender_3
  assign and_2_out = {16{1'b1}} & not_1_out;  // AND_Gate and_2, 16 bits wide
  assign not_1_out = ~subtractor_1_out;  // NOT_Gate not_1, 16 bits wide
  Multiplexer #(.enable("false"), .select(3), .width(16)) multiplexer_1 (
    .in0(shifter_1_out), .in1(shifter_2_out), .in2(adder_1_out), .in3(and_1_out), .in4(or_1_out),
    .in5(xor_1_out), .in6(bit_extender_3_out), .in7(multiplier_1_out), .out(Result), .sel(Switch));
  and and_3 (Equal, and_2_out[0], and_2_out[1], and_2_out[2], and_2_out[3], and_2_out[4], and_2_out[5], and_2_out[6], and_2_out[7], and_2_out[8], and_2_out[9], and_2_out[10], and_2_out[11], and_2_out[12], and_2_out[13], and_2_out[14], and_2_out[15]);

  // Other names for the same wires on the sheet: result_2[15:0] = Result_2_a9898de3; S[2:0] = Switch

  // Notes on the sheet:
  //   INPUTS to your circuit
  //   DON'T CHANGE THE LOCATIONS OF THE INPUTS AND OUTPUTS!
  //   OUTPUTS from your circuit
endmodule
