// Logisim project regfile.circ as structural Verilog: 2 circuits, main circuit main
module main (
  input  [2:0] Read_Register_1_eca808b4,
  input  [2:0] Read_Register_2_4b336a3e,
  input  [2:0] Write_Register_1c78e1ef,
  input  [15:0] Write_Data_00073c80,
  input  Write_Enable_5f560963,
  input  Clock,
  output [15:0] L_s0_Value_3e1de553,
  output [15:0] L_s1_Value_f16d02bf,
  output [15:0] L_s2_Value_6a9ed51f,
  output [15:0] L_ra_Value_b804995d,
  output [15:0] L_sp_Value_269f0ffd,
  output [15:0] Read_Data_1_c47ea0d8,
  output [15:0] Read_Data_2_34b29906
);

  wire and_1_out, and_2_out, and_3_out, and_4_out, and_5_out, and_6_out, and_7_out, write_reg1, write_reg2,
       write_reg3, write_reg4, write_reg5, write_reg6, write_reg7;
  wire [15:0] data_reg0, data_reg5, data_reg6;

  and and_1 (and_1_out, write_reg1, Write_Enable_5f560963);
  and and_2 (and_2_out, write_reg2, Write_Enable_5f560963);
  and and_3 (and_3_out, write_reg3, Write_Enable_5f560963);
  Register #(.width(16)) register_1 (.D(Write_Data_00073c80), .en(1'b0), .clk(Clock), .Q(data_reg0));  // open: clr
  Register #(.width(16)) register_2 (
    .D(Write_Data_00073c80), .en(and_1_out), .clk(Clock), .Q(L_ra_Value_b804995d));  // open: clr
  Register #(.width(16)) register_3 (
    .D(Write_Data_00073c80), .en(and_2_out), .clk(Clock), .Q(L_s0_Value_3e1de553));  // open: clr
  Register #(.width(16)) register_4 (
    .D(Write_Data_00073c80), .en(and_3_out), .clk(Clock), .Q(L_s1_Value_f16d02bf));  // open: clr
  and and_4 (and_4_out, write_reg4, Write_Enable_5f560963);
  and and_5 (and_5_out, write_reg5, Write_Enable_5f560963);
  and and_6 (and_6_out, write_reg6, Write_Enable_5f560963);
  and and_7 (and_7_out, write_reg7, Write_Enable_5f560963);
  Register #(.width(16)) register_5 (
    .D(Write_Data_00073c80), .en(and_4_out), .clk(Clock), .Q(L_s2_Value_6a9ed51f));  // open: clr
  Register #(.width(16)) register_6 (.D(Write_Data_00073c80), .en(and_5_out), .clk(Clock), .Q(data_reg5));  // open: clr
  Register #(.width(16)) register_7 (.D(Write_Data_00073c80), .en(and_6_out), .clk(Clock), .Q(data_reg6));  // open: clr
  Register #(.width(16)) register_8 (
    .D(Write_Data_00073c80), .en(and_7_out), .clk(Clock), .Q(L_sp_Value_269f0ffd));  // open: clr
  control_unit control_unit_1 (
    .data_reg0(data_reg0), .data_reg1(L_ra_Value_b804995d), .data_reg2(L_s0_Value_3e1de553),
    .data_reg3(L_s1_Value_f16d02bf), .data_reg4(L_s2_Value_6a9ed51f), .data_reg5(data_reg5),
    .data_reg6(data_reg6), .data_reg7(L_sp_Value_269f0ffd), .read_sel1(Read_Register_1_eca808b4),
    .read_sel2(Read_Register_2_4b336a3e), .write_sel(Write_Register_1c78e1ef),
    .read_data1(Read_Data_1_c47ea0d8), .read_data2(Read_Data_2_34b29906), .write_reg1(write_reg1),
    .write_reg2(write_reg2), .write_reg3(write_reg3), .write_reg4(write_reg4), .write_reg5(write_reg5),
    .write_reg6(write_reg6), .write_reg7(write_reg7));

  // Other names for the same wires on the sheet: clk = Clock; data_reg1[15:0] = L_ra_Value_b804995d;
  //   data_reg2[15:0] = L_s0_Value_3e1de553; data_reg3[15:0] = L_s1_Value_f16d02bf;
  //   data_reg4[15:0] = L_s2_Value_6a9ed51f; data_reg7[15:0] = L_sp_Value_269f0ffd;
  //   read_data1[15:0] = Read_Data_1_c47ea0d8; read_data2[15:0] = Read_Data_2_34b29906;
  //   read_reg1[2:0] = Read_Register_1_eca808b4; read_reg2[2:0] = Read_Register_2_4b336a3e;
  //   write_data[15:0] = Write_Data_00073c80; write_en = Write_Enable_5f560963;
  //   write_reg[2:0] = Write_Register_1c78e1ef

  // Notes on the sheet:
  //   INPUTS to your circuit
  //   DON'T CHANGE THE LOCATIONS OF THE INPUTS AND OUTPUTS!
  //   These are DEBUG/TEST outputs from your circuit.
  //   OUTPUTS from your circuit
endmodule

module control_unit (
  input  [15:0] data_reg0,
  input  [15:0] data_reg1,
  input  [15:0] data_reg2,
  input  [15:0] data_reg3,
  input  [15:0] data_reg4,
  input  [15:0] data_reg5,
  input  [15:0] data_reg6,
  input  [15:0] data_reg7,
  input  [2:0] read_sel1,
  input  [2:0] read_sel2,
  input  [2:0] write_sel,
  output [15:0] read_data1,
  output [15:0] read_data2,
  output write_reg1,
  output write_reg2,
  output write_reg3,
  output write_reg4,
  output write_reg5,
  output write_reg6,
  output write_reg7
);

  Demultiplexer #(.enable("false"), .select(3)) demultiplexer_1 (
    .out1(write_reg1), .out2(write_reg2), .out3(write_reg3), .out4(write_reg4), .out5(write_reg5),
    .out6(write_reg6), .out7(write_reg7), .in(1'b1), .sel(write_sel));  // open: out0
  Multiplexer #(.enable("false"), .select(3), .width(16)) multiplexer_1 (
    .in0(data_reg0), .in1(data_reg1), .in2(data_reg2), .in3(data_reg3), .in4(data_reg4), .in5(data_reg5),
    .in6(data_reg6), .in7(data_reg7), .out(read_data1), .sel(read_sel1));
  Multiplexer #(.enable("false"), .select(3), .width(16)) multiplexer_2 (
    .in0(data_reg0), .in1(data_reg1), .in2(data_reg2), .in3(data_reg3), .in4(data_reg4), .in5(data_reg5),
    .in6(data_reg6), .in7(data_reg7), .out(read_data2), .sel(read_sel2));
endmodule
